# Fritzing sketch HWSchema (saved by Fritzing 0.9.3b)

parts:
  U1 = ESP8266 WiFi Module [part_number=ESP8266]
  Componente2 = Bluetooth HC-05 Macho
  BAT1 = BC9VPC [package=bc9vpc]
  Componente4 = TFT 1.8 inch 160x128 w microSD [part_number=358]
  IC2 = Voltage Regulator Tinxi AMS1117 [package=sot223]
  IC1 = Voltage Regulator Tinxi AMS1117 [package=sot223]
  R1 = Resistor [tolerance=±5% resistance=1k package=THT]
  R2 = Resistor [tolerance=±5% resistance=2k package="2010 [SMD]"]
  R3 = Resistor [tolerance=±5% resistance=1k package=THT]
  R4 = Resistor [tolerance=±5% resistance=2k package="2010 [SMD]"]
  Componente3 = Arduino Mega 2560 (Rev3)
  R5 = Resistor [tolerance=±5% resistance=1k package=THT]
  R6 = Resistor [tolerance=±5% resistance=2k package="2010 [SMD]"]

nets:
  N1: U1.RXD, R3.Pin_1, R4.Pin_0
  N2: U1.VCC, U1.CH_PD, IC2.VCC_OUT
  GND: U1.GPIO_0, U1.GPIO_2, U1.GND, Componente2.GND, BAT1.V-, Componente4.GND, IC2.GND_IN, IC2.GND_OUT, IC1.GND_IN, IC1.GND_OUT, R2.Pin_1, R4.Pin_1, Componente3.GND, R6.Pin_1
  N3: U1.TXD, Componente3.D19/RX1
  N4: Componente2.TXD, Componente3.D15/RX3
  N5: Componente2.RXD, R1.Pin_1, R2.Pin_0
  N6: Componente2.VCC, IC1.VCC_OUT
  N7: Componente2.Key, R5.Pin_1, R6.Pin_0
  N8: BAT1.V+, IC2.VCC_IN, IC1.VCC_IN, Componente3.VIN
  N9: Componente4.MOSI, Componente3.D53
  N10: Componente4.TFTCS, Componente3.D48
  N11: Componente4.CARDCS, Componente3.D49
  N12: Componente4.TFTDC, Componente3.D51
  N13: Componente4.RESET, Componente3.D52
  +5V: Componente4.+5V, Componente3.5V
  N14: R1.Pin_0, Componente3.D14/TX3
  N15: R3.Pin_0, Componente3.D18/TX1
  N16: Componente3.D7_PWM, R5.Pin_0

custom parts:
  ESP8266 WiFi Module: Generic WiFi Module based on the ESP8266 with onboard PCB antenna and UART communications
  TFT 1.8 inch 160x128 w microSD: This lovely little display breakout is the best way to add a small, colorful and bright display to any project. Since the display uses 4-wire SPI to communicate and has its own pixel-addressable frame buffer, it can be used with every kind of microcontroller. Even a very small one with low memory and few pins available! The 1.8" display has 128x160 color pixels.
